# Fritzing sketch g-c-c (saved by Fritzing 0.9.3b)
breadboards: 1

parts:
  Raspberry_Pi_1 = Raspberry Pi 3 [part_number=RPI-3-V1.2]
  R1 = Resistor [tolerance=±5% resistance=470 package=THT]
  S1 = Pushbutton [package="[THT]"]
  S2 = Pushbutton [package="[THT]"]
  S3 = Pushbutton [package="[THT]"]
  S4 = Pushbutton [package="[THT]"]
  S5 = Pushbutton [package="[THT]"]
  S6 = Pushbutton [package="[THT]"]
  U1 = WS2812 RGB LED strip
  U2 = WS2812 RGB LED strip
  VCC1 = 4 x AAA Battery Mount
  VCC2 = 4 x AAA Battery Mount

nets:
  N1: Raspberry_Pi_1.GND, S1.Pin_1, S1.Pin_2, S2.Pin_1, S2.Pin_2, S3.Pin_1, S3.Pin_2, S4.Pin_1, S4.Pin_2, S5.Pin_1, S5.Pin_2, S6.Pin_1, S6.Pin_2, U1.GND#0, VCC1.-
  N2: Raspberry_Pi_1.GPIO17, S5.Pin_3, S5.Pin_4
  N3: Raspberry_Pi_1.GPIO27, S6.Pin_3, S6.Pin_4
  N4: Raspberry_Pi_1.GPIO21, S4.Pin_3, S4.Pin_4
  N5: Raspberry_Pi_1.GPIO25, S3.Pin_3, S3.Pin_4
  N6: Raspberry_Pi_1.GPIO24, S2.Pin_3, S2.Pin_4
  N7: Raspberry_Pi_1.GPIO23, S1.Pin_3, S1.Pin_4
  N8: Raspberry_Pi_1.GPIO18, R1.Pin_1
  N9: R1.Pin_0, U1.DIN
  N10: U1.GND#4, U2.GND, VCC2.-
  N11: U1.DOUT, U2.DIN

notes:
  SK6812 Streifen für Display 1 (Grün)
  SK6812 Streifen für Display 2 (Rot)
  Reset, Start, Zeit, Increment Taster zum
  Einstellen des Betriebsmodus sind im Gehäuse der Kontrolleinheit verbaut
  Grüner und Roter Riesentaster werden per RJ-45 Kabel mit der Kontrolleinheit verbunden
  Beide Displays haben eine separate Stromversorgung, Ebenso der Raspberry Pi (über Micro-USB - hier nicht eingezeichnet). Das GND Niveau der LED Streifen muss gleich sein, daher wird neben dem Signal auch GND vom ersten Display zum 2. Display per RJ-45 Kabel "durchverbunden". Ebenso wird GND vom Raspi mit GND des 1. Displays verbunden.
  Es werden die internen Pull-Up Widerstände des Raspis genutzt. Nur ein 470 Ohm Wellenwiderstand für den LED Streifen ist notwendig.
  Verbindung zwischen Kontrolleinheit und Display 1 erfolgt per RJ-45 Kabel

custom parts:
  WS2812 RGB LED strip: WS2812 strip
